# Fritzing sketch batteryPower (saved by Fritzing 0.9.3b)
stripboards: 1

parts:
  Mot1 = Moteino R4
  VCC1 = Battery
  RHT1 = Humidity and Temperature Sensor RHT03
  R1 = Resistor [tolerance=±5% resistance=220 package=THT]

nets:
  N1: Mot1.GND, VCC1.-, RHT1.GND_2
  N2: Mot1.VIN, VCC1.+
  N3: Mot1.A5, RHT1.Data-signal, R1.Pin_0
  N4: Mot1.A2, RHT1.Vcc, R1.Pin_1

custom parts:
  Moteino R4: Low Power Lab's Moteino
