# Fritzing sketch wiredPower (saved by Fritzing 0.9.3b)
stripboards: 7

parts:
  DHT1 = DHT22 Humidity and Temperature Sensor
  DHT2 = DHT22 Humidity and Temperature Sensor
  DHT3 = DHT22 Humidity and Temperature Sensor
  DHT4 = DHT22 Humidity and Temperature Sensor
  DHT5 = DHT22 Humidity and Temperature Sensor
  DHT6 = DHT22 Humidity and Temperature Sensor
  Mot1 = Moteino R4
  R1 = Resistor [tolerance=±5% resistance=220 package=THT]
  R2 = Resistor [tolerance=±5% resistance=220 package=THT]
  R3 = Resistor [tolerance=±5% resistance=220 package=THT]
  R4 = Resistor [tolerance=±5% resistance=220 package=THT]
  R5 = Resistor [tolerance=±5% resistance=220 package=THT]
  R6 = Resistor [tolerance=±5% resistance=220 package=THT]
  Part1 = USB Mini-B Breakout [part_number=1764]

nets:
  VDD: DHT1.VDD, DHT2.VDD, DHT3.VDD, DHT4.VDD, Mot1.VIN, Part1.5V
  N1: DHT1.DATA, Mot1.A0, R1.Pin_1
  GND: DHT1.GND, DHT2.GND, DHT3.GND, DHT4.GND, Mot1.GND, Part1.GND
  N2: DHT2.DATA, Mot1.A1, R2.Pin_1
  N3: DHT3.DATA, Mot1.A2, R3.Pin_1
  N4: DHT4.DATA, Mot1.A3, R4.Pin_1
  N5: DHT5.DATA, Mot1.A4, R5.Pin_1
  N6: DHT6.DATA, Mot1.A5, R6.Pin_1

notes:
  3.3V, GND, Data all in conduit
  DHT22 and connections in
  a small box

custom parts:
  Moteino R4: Low Power Lab's Moteino
  USB Mini-B Breakout: Simple but effective - this breakout board has a USB Mini-B connector, with all 5 pins broken out. Great for pairing with a microcontroller with USB support, or adding USB 5V power to a project.
