# Fritzing sketch wiredPowerProtoBoard (saved by Fritzing 0.9.3b)
perfboards: 9

parts:
  Mot1 = Moteino R4
  Part1 = adafruit [part_number=1764]
  R1 = Resistor [tolerance=±5% resistance=220 package=THT]
  RHT1 = Humidity and Temperature Sensor RHT03
  RHT2 = Humidity and Temperature Sensor RHT03
  R2 = Resistor [tolerance=±5% resistance=220 package=THT]
  R3 = Resistor [tolerance=±5% resistance=220 package=THT]
  RHT3 = Humidity and Temperature Sensor RHT03
  R4 = Resistor [tolerance=±5% resistance=220 package=THT]
  RHT4 = Humidity and Temperature Sensor RHT03
  R5 = Resistor [tolerance=±5% resistance=220 package=THT]
  RHT5 = Humidity and Temperature Sensor RHT03
  RHT6 = Humidity and Temperature Sensor RHT03
  R6 = Resistor [tolerance=±5% resistance=220 package=THT]
  R7 = Resistor [tolerance=±5% resistance=220 package=THT]
  RHT7 = Humidity and Temperature Sensor RHT03
  R8 = Resistor [tolerance=±5% resistance=220 package=THT]
  RHT8 = Humidity and Temperature Sensor RHT03

nets:
  N1: Mot1.A5, R2.Pin_1, RHT3.Data-signal
  N2: Mot1.A4, R4.Pin_1, RHT4.Data-signal
  N3: Mot1.A3, R5.Pin_1, RHT5.Data-signal
  N4: Mot1.A2, RHT6.Data-signal, R6.Pin_1
  N5: Mot1.A1, R7.Pin_1, RHT7.Data-signal
  N6: Mot1.A0, R8.Pin_1, RHT8.Data-signal
  N7: Part1.connector7, RHT1.GND_2, RHT2.GND_2, RHT3.GND_2, RHT4.GND_2, RHT5.GND_2, RHT6.GND_2, RHT7.GND_2, RHT8.GND_2
  VCC: Part1.connector11, R1.Pin_0, RHT1.Vcc, RHT2.Vcc, RHT3.Vcc, RHT4.Vcc, RHT5.Vcc, RHT6.Vcc, RHT7.Vcc, RHT8.Vcc
  N8: RHT2.Data-signal, R3.Pin_1
  N9: R2.Pin_0, R3.Pin_0, R4.Pin_0, R5.Pin_0, R6.Pin_0, R7.Pin_0, R8.Pin_0

notes:
  = solder bridge
  = jumper wire

custom parts:
  Moteino R4: Low Power Lab's Moteino
