# Fritzing sketch wiredPower (saved by Fritzing 0.9.3b)
stripboards: 4

parts:
  Mot1 = Moteino R4
  DHT1 = DHT22 Humidity and Temperature Sensor
  R1 = Resistor [tolerance=±5% resistance=220 package=THT]
  DHT2 = DHT22 Humidity and Temperature Sensor
  R2 = Resistor [tolerance=±5% resistance=220 package=THT]
  DHT3 = DHT22 Humidity and Temperature Sensor
  R3 = Resistor [tolerance=±5% resistance=220 package=THT]
  VCC1 = 4 x AAA Battery Mount

nets:
  VDD: Mot1.3v3, DHT1.VDD, R1.Pin_0, DHT2.VDD, R2.Pin_0, DHT3.VDD, R3.Pin_0, VCC1.+
  N1: Mot1.A4, DHT3.DATA, R3.Pin_1
  N2: Mot1.A3, DHT2.DATA, R2.Pin_1
  N3: Mot1.A2, DHT1.DATA, R1.Pin_1
  GND: DHT2.GND, DHT3.GND, VCC1.-

notes:
  These wires will all be encased together in metal conduit
  These should be encased or atleast wrapped in electrical tape

custom parts:
  Moteino R4: Low Power Lab's Moteino
